// Logisim project digital circuit.circ as structural Verilog: 1 circuit, main circuit main
module main (
  input  in_1,
  input  in_2,
  input  in_3
);

  wire and_1_out, and_2_out, and_3_out, clock_1_out, not_1_out, not_2_out, not_3_out, or_1_out, or_2_out,
       or_3_out;

  not not_1 (not_1_out, in_3);
  not not_2 (not_2_out, in_2);
  not not_3 (not_3_out, in_1);
  and and_1 (and_1_out, in_1, not_2_out, not_1_out);
  and and_2 (and_2_out, not_3_out, in_2, not_1_out);
  and and_3 (and_3_out, not_3_out, not_2_out, in_3);
  or or_1 (or_1_out, and_2_out, and_3_out);
  or or_2 (or_2_out, and_1_out, and_3_out);
  or or_3 (or_3_out, and_2_out, and_1_out);
  J_K_Flip_Flop j_k_ff_1 (.J(and_1_out), .clk(clock_1_out), .K(or_1_out));  // open: Q, Qn, preset, en, reset
  J_K_Flip_Flop j_k_ff_2 (.J(and_2_out), .clk(clock_1_out), .K(or_2_out));  // open: Q, Qn, preset, en, reset
  J_K_Flip_Flop j_k_ff_3 (.J(and_3_out), .clk(clock_1_out), .K(or_3_out));  // open: Q, Qn, preset, en, reset
  Clock clock_1 (.out(clock_1_out));
endmodule
