// Logisim project digitalcircuit2.circ as structural Verilog: 1 circuit, main circuit main
module main (
  input  in_1,
  input  in_2,
  input  in_3,
  input  in_4,
  input  in_5
);

  wire and_1_out, clock_1_out, comparator_1_eq, decoder_1_out0, decoder_1_out1, decoder_1_out2,
       decoder_1_out3, decoder_1_out4, multiplexer_1_out, not_1_out;
  wire [2:0] counter_1_q, register_1_q, register_2_q;

  Clock clock_1 (.out(clock_1_out));
  Counter #(.width(3), .max('h4), .trigger("falling")) counter_1 (
    .Q(counter_1_q), .clk(clock_1_out));  // open: load, D, count, carry, clr
  Multiplexer #(.select(3)) multiplexer_1 (
    .in0(in_1), .in1(in_2), .in2(in_3), .in3(in_4), .in4(in_5), .in5(1'b0), .in6(1'b0), .in7(1'b0),
    .out(multiplexer_1_out), .sel(counter_1_q), .en(1'b1));
  not not_1 (not_1_out, multiplexer_1_out);
  Register #(.width(3)) register_1 (
    .D(counter_1_q), .en(multiplexer_1_out), .Q(register_1_q), .clk(clock_1_out));  // open: clr
  and and_1 (and_1_out, comparator_1_eq, not_1_out);
  Register #(.width(3)) register_2 (
    .D(register_1_q), .en(and_1_out), .Q(register_2_q), .clk(clock_1_out));  // open: clr
  Decoder #(.select(3)) decoder_1 (
    .out0(decoder_1_out0), .out1(decoder_1_out1), .out2(decoder_1_out2), .out3(decoder_1_out3),
    .out4(decoder_1_out4), .sel(register_2_q));  // open: out5, out6, out7, en
  LED led_1 (.in(decoder_1_out0));
  LED led_2 (.in(decoder_1_out1));
  LED led_3 (.in(decoder_1_out2));
  LED led_4 (.in(decoder_1_out3));
  LED led_5 (.in(decoder_1_out4));
  Comparator #(.width(3)) comparator_1 (.a(register_2_q), .b(counter_1_q), .eq(comparator_1_eq));  // open: gt, lt

  // Notes on the sheet:
  //   counter
  //   next
  //   current
endmodule
